// Logisim project cpu.circ as structural Verilog: 14 circuits, main circuit main
module main (
  input  [15:0] in_1,
  input  R
);

  wire add, addi, and_, ble, bne, clk, input_, Itype, j, jal, jr, Jtype, keyboard_1_avail, lw,
       memory_latch_1_oe_latched, memory_latch_1_we_latched, not_, not_1_out, not_2_out, not_4_out, or_4_out,
       or_6_out, output_, RegWE, Rtype, sll_, srl_, sub, sw;
  wire [2:0] multiplexer_2_out, OpType, WReg;
  wire [7:0] KeyboardData;
  wire [11:0] Address;
  wire [15:0] ALUData, D1, D2, memory_latch_1_address_latched, memory_latch_1_data_in_latched,
       multiplexer_1_out, multiplexer_3_out, multiplexer_4_out, multiplexer_6_out, multiplexer_7_out,
       multiplexer_8_out, multiplexer_9_out, my_alu_1_outputdata, my_alu_3_outputdata, PC, RAMData, WData;
  wire [15:12] I;

  Clock clock_1 (.out(clk));
  Decoder #(.select(4)) decoder_1 (
    .out0(add), .out1(addi), .out2(sub), .out3(sll_), .out4(srl_), .out5(and_), .out6(not_), .out7(lw),
    .out8(sw), .out9(bne), .out10(ble), .out11(j), .out12(jr), .out13(jal), .out14(input_), .out15(output_),
    .sel(I));  // open: en
  or or_1 (Jtype, j, jal);
  or or_2 (Rtype, add, sub, sll_, srl_, and_, not_, jr);
  or or_3 (Itype, addi, lw, sw, bne, ble, input_, output_);
  my_ALU my_alu_1 (.OutputData(my_alu_1_outputdata), .InputData2(PC), .InputData1(16'h1), .OpType(3'b000));
  Multiplexer #(.width(16), .enable("false")) multiplexer_1 (
    .in0(D2), .in1({{10{1'b0}}, Address[5:0]}), .out(multiplexer_1_out), .sel(Itype));
  Multiplexer #(.width(3), .enable("false")) multiplexer_2 (
    .in0(Address[5:3]), .in1(Address[8:6]), .out(multiplexer_2_out), .sel(Itype));
  Multiplexer #(.width(16), .enable("false")) multiplexer_3 (
    .in0(my_alu_1_outputdata), .in1({4'b0000, Address}), .out(multiplexer_3_out), .sel(Jtype));
  Multiplexer #(.width(16), .enable("false")) multiplexer_4 (
    .in0(multiplexer_1_out), .in1(16'h1), .out(multiplexer_4_out), .sel(jal));
  or or_4 (or_4_out, sll_, srl_);
  Multiplexer #(.width(3), .enable("false")) multiplexer_5 (
    .in0(multiplexer_2_out), .in1(3'b111), .out(WReg), .sel(jr));
  not not_1 (not_1_out, clk);
  Multiplexer #(.width(16), .enable("false")) multiplexer_6 (
    .in0(multiplexer_3_out), .in1(D1), .out(multiplexer_6_out), .sel(jr));
  Multiplexer #(.width(16), .enable("false")) multiplexer_7 (.in0(D1), .in1(PC), .out(multiplexer_7_out), .sel(jal));
  Multiplexer #(.width(16), .enable("false")) multiplexer_8 (
    .in0(multiplexer_4_out), .in1({{13{1'b0}}, Address[2:0]}), .out(multiplexer_8_out), .sel(or_4_out));
  or or_5 (RegWE, add, addi, sub, sll_, srl_, and_, not_, lw, jal, input_);
  // Probe on PC
  my_register PCRegister (.D(multiplexer_6_out), .clk(not_1_out), .R(R), .Q(PC));
  TTY #(.rows(13), .cols(80)) tty_1 (.data(D1[6:0]), .clk(clk), .we(output_), .clr(R));
  Multiplexer #(.width(16), .enable("false")) multiplexer_9 (
    .in0(ALUData), .in1(RAMData), .out(multiplexer_9_out), .sel(lw));
  Keyboard keyboard_1 (.clk(not_2_out), .re(input_), .avail(keyboard_1_avail), .data(KeyboardData[6:0]));  // open: clr
  not not_2 (not_2_out, clk);
  Multiplexer #(.width(16), .enable("false")) multiplexer_10 (
    .in0(multiplexer_9_out), .in1({{8{1'b0}}, KeyboardData}), .out(WData), .sel(input_));
  my_ALU my_alu_2 (
    .OutputData(ALUData), .InputData2(multiplexer_8_out), .InputData1(multiplexer_7_out), .OpType(OpType));
  or or_6 (or_6_out, add, addi, jal);
  assign OpType = srl_ ? 3'b101 : 3'bz;  // Controlled_Buffer controlled_buffer_1
  not not_3 (KeyboardData[7], keyboard_1_avail);
  // Probe on D1
  RegisterFile registerfile_1 (
    .WriteData(WData), .WriteReg(WReg), .ReadReg2(Address[8:6]), .ReadReg1(Address[11:9]),
    .RegWriteEnable(RegWE), .Reset(R), .clk(clk), .ReadData1(D1), .ReadData2(D2));
  // Probe on D2
  assign OpType = and_ ? 3'b010 : 3'bz;  // Controlled_Buffer controlled_buffer_2
  assign OpType = not_ ? 3'b011 : 3'bz;  // Controlled_Buffer controlled_buffer_3
  assign OpType = sll_ ? 3'b100 : 3'bz;  // Controlled_Buffer controlled_buffer_4
  assign OpType = or_6_out ? 3'b000 : 3'bz;  // Controlled_Buffer controlled_buffer_5
  assign OpType = sub ? 3'b001 : 3'bz;  // Controlled_Buffer controlled_buffer_6
  // Probe on {{8{1'b0}}, KeyboardData}
  ROM #(.addrWidth(16), .dataWidth(16)) rom_1 (.addr(PC), .data({I, Address}));
  my_ALU my_alu_3 (
    .OutputData(my_alu_3_outputdata), .InputData2({{10{1'b0}}, Address[5:0]}), .InputData1(D1),
    .OpType(3'b000));
  not not_4 (not_4_out, clk);
  RAM #(.addrWidth(16), .dataWidth(16), .trigger("high"), .databus("bibus")) ram_1 (
    .addr(memory_latch_1_address_latched), .we(memory_latch_1_we_latched), .oe(memory_latch_1_oe_latched),
    .din(memory_latch_1_data_in_latched), .dout(RAMData));
  memory_latch memory_latch_1 (
    .OE_latched(memory_latch_1_oe_latched), .WE_latched(memory_latch_1_we_latched),
    .address_latched(memory_latch_1_address_latched), .data_in(D2), .clk(not_4_out), .WE(sw),
    .address(my_alu_3_outputdata), .data_in_latched(memory_latch_1_data_in_latched));

  // Other names for the same wires on the sheet: I[11:0] = Address; Rt[2:0] = Address[8:6]; Rs[2:0] = Address[11:9];
  //   Immed[5:0] = Address[5:0]; Shamt[2:0] = Address[2:0]; Rd[2:0] = Address[5:3]; Opcode[3:0] = I

  // Notes on the sheet:
  //   contents of rom_1 (hex, n*v repeats v):
  //   1111 0 1111
endmodule

module my_register (
  input  clk,
  input  R,
  input  [15:0] D,
  output [15:0] Q
);

  D_Flip_Flop d_ff_1 (.D(D[0]), .clk(clk), .Q(Q[0]), .reset(R));  // open: Qn, preset
  D_Flip_Flop d_ff_2 (.D(D[1]), .clk(clk), .Q(Q[1]), .reset(R));  // open: Qn, preset
  D_Flip_Flop d_ff_3 (.D(D[2]), .clk(clk), .Q(Q[2]), .reset(R));  // open: Qn, preset
  D_Flip_Flop d_ff_4 (.D(D[3]), .clk(clk), .Q(Q[3]), .reset(R));  // open: Qn, preset
  D_Flip_Flop d_ff_5 (.D(D[4]), .clk(clk), .Q(Q[4]), .reset(R));  // open: Qn, preset
  D_Flip_Flop d_ff_6 (.D(D[5]), .clk(clk), .Q(Q[5]), .reset(R));  // open: Qn, preset
  D_Flip_Flop d_ff_7 (.D(D[6]), .clk(clk), .Q(Q[6]), .reset(R));  // open: Qn, preset
  D_Flip_Flop d_ff_8 (.D(D[7]), .clk(clk), .Q(Q[7]), .reset(R));  // open: Qn, preset
  D_Flip_Flop d_ff_9 (.D(D[8]), .clk(clk), .Q(Q[8]), .reset(R));  // open: Qn, preset
  D_Flip_Flop d_ff_10 (.D(D[9]), .clk(clk), .Q(Q[9]), .reset(R));  // open: Qn, preset
  D_Flip_Flop d_ff_11 (.D(D[10]), .clk(clk), .Q(Q[10]), .reset(R));  // open: Qn, preset
  D_Flip_Flop d_ff_12 (.D(D[11]), .clk(clk), .Q(Q[11]), .reset(R));  // open: Qn, preset
  D_Flip_Flop d_ff_13 (.D(D[12]), .clk(clk), .Q(Q[12]), .reset(R));  // open: Qn, preset
  D_Flip_Flop d_ff_14 (.D(D[13]), .clk(clk), .Q(Q[13]), .reset(R));  // open: Qn, preset
  D_Flip_Flop d_ff_15 (.D(D[14]), .clk(clk), .Q(Q[14]), .reset(R));  // open: Qn, preset
  D_Flip_Flop d_ff_16 (.D(D[15]), .clk(clk), .Q(Q[15]), .reset(R));  // open: Qn, preset
endmodule

module RegisterFile (
  input  clk,
  input  Reset,
  input  RegWriteEnable,
  input  [2:0] ReadReg1,
  input  [2:0] ReadReg2,
  input  [2:0] WriteReg,
  input  [15:0] WriteData,
  output [15:0] ReadData1,
  output [15:0] ReadData2
);

  wire decoder_1_out0, decoder_1_out1, decoder_1_out2, decoder_1_out3, decoder_1_out4, decoder_1_out5,
       decoder_1_out6, decoder_1_out7;
  wire [15:0] multiplexer_1_out, multiplexer_2_out, multiplexer_3_out, multiplexer_4_out, multiplexer_5_out,
       multiplexer_6_out, multiplexer_7_out, multiplexer_8_out, Q0, Q1, Q2, Q3, Q4, Q5, Q6, Q7;

  my_mux my_mux_1 (.I6(Q6), .I4(Q4), .I2(Q2), .I3(Q3), .I5(Q5), .I7(Q7), .I1(Q1), .I0(Q0), .S(ReadReg1), .O(ReadData1));
  my_mux my_mux_2 (.I6(Q6), .I4(Q4), .I2(Q2), .I3(Q3), .I5(Q5), .I7(Q7), .I1(Q1), .I0(Q0), .S(ReadReg2), .O(ReadData2));
  Decoder #(.select(3)) decoder_1 (
    .out0(decoder_1_out0), .out1(decoder_1_out1), .out2(decoder_1_out2), .out3(decoder_1_out3),
    .out4(decoder_1_out4), .out5(decoder_1_out5), .out6(decoder_1_out6), .out7(decoder_1_out7),
    .sel(WriteReg), .en(RegWriteEnable));
  Multiplexer #(.width(16), .enable("false")) multiplexer_1 (
    .in0(Q0), .in1(WriteData), .out(multiplexer_1_out), .sel(decoder_1_out0));
  // Probe on Q0
  my_register my_register_1 (.D(multiplexer_1_out), .clk(clk), .R(Reset), .Q(Q0));
  Multiplexer #(.width(16), .enable("false")) multiplexer_2 (
    .in0(Q1), .in1(WriteData), .out(multiplexer_2_out), .sel(decoder_1_out1));
  // Probe on Q1
  my_register my_register_2 (.D(multiplexer_2_out), .clk(clk), .R(Reset), .Q(Q1));
  Multiplexer #(.width(16), .enable("false")) multiplexer_3 (
    .in0(Q2), .in1(WriteData), .out(multiplexer_3_out), .sel(decoder_1_out2));
  // Probe on Q2
  my_register my_register_3 (.D(multiplexer_3_out), .clk(clk), .R(Reset), .Q(Q2));
  Multiplexer #(.width(16), .enable("false")) multiplexer_4 (
    .in0(Q3), .in1(WriteData), .out(multiplexer_4_out), .sel(decoder_1_out3));
  // Probe on Q3
  my_register my_register_4 (.D(multiplexer_4_out), .clk(clk), .R(Reset), .Q(Q3));
  Multiplexer #(.width(16), .enable("false")) multiplexer_5 (
    .in0(Q4), .in1(WriteData), .out(multiplexer_5_out), .sel(decoder_1_out4));
  my_register my_register_5 (.D(multiplexer_5_out), .clk(clk), .R(Reset), .Q(Q4));
  // Probe on Q4
  Multiplexer #(.width(16), .enable("false")) multiplexer_6 (
    .in0(Q5), .in1(WriteData), .out(multiplexer_6_out), .sel(decoder_1_out5));
  // Probe on Q5
  my_register my_register_6 (.D(multiplexer_6_out), .clk(clk), .R(Reset), .Q(Q5));
  Multiplexer #(.width(16), .enable("false")) multiplexer_7 (
    .in0(Q6), .in1(WriteData), .out(multiplexer_7_out), .sel(decoder_1_out6));
  // Probe on Q6
  my_register my_register_7 (.D(multiplexer_7_out), .clk(clk), .R(Reset), .Q(Q6));
  Multiplexer #(.width(16), .enable("false")) multiplexer_8 (
    .in0(Q7), .in1(WriteData), .out(multiplexer_8_out), .sel(decoder_1_out7));
  // Probe on Q7
  my_register my_register_8 (.D(multiplexer_8_out), .clk(clk), .R(Reset), .Q(Q7));

  // Other names for the same wires on the sheet: R = Reset; RR1[2:0] = ReadReg1; RR2[2:0] = ReadReg2;
  //   WD[15:0] = WriteData; WE = RegWriteEnable; WR[2:0] = WriteReg
endmodule

module my_mux (
  input  [15:0] I0,
  input  [15:0] I1,
  input  [15:0] I2,
  input  [15:0] I3,
  input  [15:0] I4,
  input  [15:0] I5,
  input  [15:0] I6,
  input  [15:0] I7,
  input  [2:0] S,
  output [15:0] O
);

  wire decoder_1_out0, decoder_1_out1, decoder_1_out2, decoder_1_out3, decoder_1_out4, decoder_1_out5,
       decoder_1_out6, decoder_1_out7;

  assign O = decoder_1_out0 ? I0 : 16'bz;  // Controlled_Buffer controlled_buffer_1
  Decoder #(.select(3)) decoder_1 (
    .out0(decoder_1_out0), .out1(decoder_1_out1), .out2(decoder_1_out2), .out3(decoder_1_out3),
    .out4(decoder_1_out4), .out5(decoder_1_out5), .out6(decoder_1_out6), .out7(decoder_1_out7), .sel(S));  // open: en
  assign O = decoder_1_out1 ? I1 : 16'bz;  // Controlled_Buffer controlled_buffer_2
  assign O = decoder_1_out2 ? I2 : 16'bz;  // Controlled_Buffer controlled_buffer_3
  assign O = decoder_1_out3 ? I3 : 16'bz;  // Controlled_Buffer controlled_buffer_4
  assign O = decoder_1_out4 ? I4 : 16'bz;  // Controlled_Buffer controlled_buffer_5
  assign O = decoder_1_out5 ? I5 : 16'bz;  // Controlled_Buffer controlled_buffer_6
  assign O = decoder_1_out6 ? I6 : 16'bz;  // Controlled_Buffer controlled_buffer_7
  assign O = decoder_1_out7 ? I7 : 16'bz;  // Controlled_Buffer controlled_buffer_8
endmodule

module my_ALU (
  input  [2:0] OpType,
  input  [15:0] InputData1,
  input  [15:0] InputData2,
  output [15:0] OutputData
);

  wire Adding, Anding, Notting, or_1_out, ShiftLeft, ShiftRight, Substracting;
  wire [15:0] ander_1_out_3, bit_shifter_left_1_out_3, bit_shifter_right_1_out_3, my_adder_1_result,
       notter_1_out_2;

  Decoder #(.select(3)) decoder_1 (
    .out0(Adding), .out1(Substracting), .out2(Anding), .out3(Notting), .out4(ShiftLeft), .out5(ShiftRight),
    .sel(OpType));  // open: out6, out7, en
  // Probe on InputData1
  // Probe on InputData2
  ander ander_1 (.out_3(ander_1_out_3), .in_2(InputData2), .in_1(InputData1));
  notter notter_1 (.in_1(InputData1), .out_2(notter_1_out_2));
  assign OutputData = Notting ? notter_1_out_2 : 16'bz;  // Controlled_Buffer controlled_buffer_1
  my_adder my_adder_1 (.A(InputData1), .B(InputData2), .sub(Substracting), .result(my_adder_1_result));  // open: ovf
  assign OutputData = Anding ? ander_1_out_3 : 16'bz;  // Controlled_Buffer controlled_buffer_2
  assign OutputData = or_1_out ? my_adder_1_result : 16'bz;  // Controlled_Buffer controlled_buffer_3
  or or_1 (or_1_out, Substracting, Adding);
  assign OutputData = ShiftRight ? bit_shifter_right_1_out_3 : 16'bz;  // Controlled_Buffer controlled_buffer_4
  bit_shifter_right bit_shifter_right_1 (.in_1(InputData2[3:0]), .in_2(InputData1), .out_3(bit_shifter_right_1_out_3));
  bit_shifter_left bit_shifter_left_1 (.in_1(InputData2[3:0]), .in_2(InputData1), .out_3(bit_shifter_left_1_out_3));
  assign OutputData = ShiftLeft ? bit_shifter_left_1_out_3 : 16'bz;  // Controlled_Buffer controlled_buffer_5
  // Probe on OutputData

  // Other names for the same wires on the sheet: A[15:0] = InputData1; B[15:0] = InputData2
endmodule

module notter (
  input  [15:0] in_1,
  output [15:0] out_2
);

  wire giant_splitter_1_o, giant_splitter_1_out_3, giant_splitter_1_out_4, giant_splitter_1_out_5,
       giant_splitter_1_out_6, giant_splitter_1_out_7, giant_splitter_1_out_8, giant_splitter_1_out_9,
       giant_splitter_1_out_10, giant_splitter_1_out_11, giant_splitter_1_out_12, giant_splitter_1_out_13,
       giant_splitter_1_out_14, giant_splitter_1_out_15, giant_splitter_1_out_16, giant_splitter_1_out_17,
       not_1_out, not_2_out, not_3_out, not_4_out, not_5_out, not_6_out, not_7_out, not_8_out, not_9_out,
       not_10_out, not_11_out, not_12_out, not_13_out, not_14_out, not_15_out, not_16_out;

  giant_splitter giant_splitter_1 (
    .out_13(giant_splitter_1_out_13), .out_12(giant_splitter_1_out_12), .out_11(giant_splitter_1_out_11),
    .out_10(giant_splitter_1_out_10), .out_9(giant_splitter_1_out_9), .out_8(giant_splitter_1_out_8),
    .out_7(giant_splitter_1_out_7), .out_6(giant_splitter_1_out_6), .out_5(giant_splitter_1_out_5),
    .out_4(giant_splitter_1_out_4), .out_3(giant_splitter_1_out_3), .O(giant_splitter_1_o), .in_1(in_1),
    .out_14(giant_splitter_1_out_14), .out_15(giant_splitter_1_out_15), .out_16(giant_splitter_1_out_16),
    .out_17(giant_splitter_1_out_17));
  not not_1 (not_1_out, giant_splitter_1_o);
  not not_2 (not_2_out, giant_splitter_1_out_3);
  not not_3 (not_3_out, giant_splitter_1_out_4);
  not not_4 (not_4_out, giant_splitter_1_out_5);
  not not_5 (not_5_out, giant_splitter_1_out_6);
  not not_6 (not_6_out, giant_splitter_1_out_7);
  not not_7 (not_7_out, giant_splitter_1_out_8);
  not not_8 (not_8_out, giant_splitter_1_out_9);
  giant_unsplitter giant_unsplitter_1 (
    .in_13(not_13_out), .in_12(not_12_out), .in_11(not_11_out), .in_10(not_10_out), .in_9(not_9_out),
    .in_8(not_8_out), .in_7(not_7_out), .in_6(not_6_out), .in_5(not_5_out), .in_4(not_4_out),
    .in_3(not_3_out), .in_2(not_2_out), .O(not_1_out), .in_14(not_14_out), .in_15(not_15_out),
    .in_16(not_16_out), .out_17(out_2));
  not not_9 (not_9_out, giant_splitter_1_out_10);
  not not_10 (not_10_out, giant_splitter_1_out_11);
  not not_11 (not_11_out, giant_splitter_1_out_12);
  not not_12 (not_12_out, giant_splitter_1_out_13);
  not not_13 (not_13_out, giant_splitter_1_out_14);
  not not_14 (not_14_out, giant_splitter_1_out_15);
  not not_15 (not_15_out, giant_splitter_1_out_16);
  not not_16 (not_16_out, giant_splitter_1_out_17);
endmodule

module ander (
  input  [15:0] in_1,
  input  [15:0] in_2,
  output [15:0] out_3
);

  wire and_1_out, and_2_out, and_3_out, and_4_out, and_5_out, and_6_out, and_7_out, and_8_out, and_9_out,
       and_10_out, and_11_out, and_12_out, and_13_out, and_14_out, and_15_out, and_16_out,
       giant_splitter_1_o, giant_splitter_1_out_3, giant_splitter_1_out_4, giant_splitter_1_out_5,
       giant_splitter_1_out_6, giant_splitter_1_out_7, giant_splitter_1_out_8, giant_splitter_1_out_9,
       giant_splitter_1_out_10, giant_splitter_1_out_11, giant_splitter_1_out_12, giant_splitter_1_out_13,
       giant_splitter_1_out_14, giant_splitter_1_out_15, giant_splitter_1_out_16, giant_splitter_1_out_17,
       giant_splitter_2_o, giant_splitter_2_out_3, giant_splitter_2_out_4, giant_splitter_2_out_5,
       giant_splitter_2_out_6, giant_splitter_2_out_7, giant_splitter_2_out_8, giant_splitter_2_out_9,
       giant_splitter_2_out_10, giant_splitter_2_out_11, giant_splitter_2_out_12, giant_splitter_2_out_13,
       giant_splitter_2_out_14, giant_splitter_2_out_15, giant_splitter_2_out_16, giant_splitter_2_out_17;

  giant_splitter giant_splitter_1 (
    .out_13(giant_splitter_1_out_13), .out_12(giant_splitter_1_out_12), .out_11(giant_splitter_1_out_11),
    .out_10(giant_splitter_1_out_10), .out_9(giant_splitter_1_out_9), .out_8(giant_splitter_1_out_8),
    .out_7(giant_splitter_1_out_7), .out_6(giant_splitter_1_out_6), .out_5(giant_splitter_1_out_5),
    .out_4(giant_splitter_1_out_4), .out_3(giant_splitter_1_out_3), .O(giant_splitter_1_o), .in_1(in_1),
    .out_14(giant_splitter_1_out_14), .out_15(giant_splitter_1_out_15), .out_16(giant_splitter_1_out_16),
    .out_17(giant_splitter_1_out_17));
  and and_1 (and_1_out, giant_splitter_1_o, giant_splitter_2_o);
  giant_splitter giant_splitter_2 (
    .out_13(giant_splitter_2_out_13), .out_12(giant_splitter_2_out_12), .out_11(giant_splitter_2_out_11),
    .out_10(giant_splitter_2_out_10), .out_9(giant_splitter_2_out_9), .out_8(giant_splitter_2_out_8),
    .out_7(giant_splitter_2_out_7), .out_6(giant_splitter_2_out_6), .out_5(giant_splitter_2_out_5),
    .out_4(giant_splitter_2_out_4), .out_3(giant_splitter_2_out_3), .O(giant_splitter_2_o), .in_1(in_2),
    .out_14(giant_splitter_2_out_14), .out_15(giant_splitter_2_out_15), .out_16(giant_splitter_2_out_16),
    .out_17(giant_splitter_2_out_17));
  and and_2 (and_2_out, giant_splitter_1_out_3, giant_splitter_2_out_3);
  and and_3 (and_3_out, giant_splitter_1_out_4, giant_splitter_2_out_4);
  and and_4 (and_4_out, giant_splitter_1_out_5, giant_splitter_2_out_5);
  and and_5 (and_5_out, giant_splitter_1_out_6, giant_splitter_2_out_6);
  and and_6 (and_6_out, giant_splitter_1_out_7, giant_splitter_2_out_7);
  and and_7 (and_7_out, giant_splitter_1_out_8, giant_splitter_2_out_8);
  and and_8 (and_8_out, giant_splitter_1_out_9, giant_splitter_2_out_9);
  and and_9 (and_9_out, giant_splitter_1_out_10, giant_splitter_2_out_10);
  and and_10 (and_10_out, giant_splitter_1_out_11, giant_splitter_2_out_11);
  and and_11 (and_11_out, giant_splitter_1_out_12, giant_splitter_2_out_12);
  and and_12 (and_12_out, giant_splitter_1_out_13, giant_splitter_2_out_13);
  and and_13 (and_13_out, giant_splitter_1_out_14, giant_splitter_2_out_14);
  and and_14 (and_14_out, giant_splitter_1_out_15, giant_splitter_2_out_15);
  and and_15 (and_15_out, giant_splitter_1_out_16, giant_splitter_2_out_16);
  and and_16 (and_16_out, giant_splitter_1_out_17, giant_splitter_2_out_17);
  giant_unsplitter giant_unsplitter_1 (
    .in_13(and_13_out), .in_12(and_12_out), .in_11(and_11_out), .in_10(and_10_out), .in_9(and_9_out),
    .in_8(and_8_out), .in_7(and_7_out), .in_6(and_6_out), .in_5(and_5_out), .in_4(and_4_out),
    .in_3(and_3_out), .in_2(and_2_out), .O(and_1_out), .in_14(and_14_out), .in_15(and_15_out),
    .in_16(and_16_out), .out_17(out_3));
endmodule

module giant_splitter (
  input  [15:0] in_1,
  output O,
  output out_3,
  output out_4,
  output out_5,
  output out_6,
  output out_7,
  output out_8,
  output out_9,
  output out_10,
  output out_11,
  output out_12,
  output out_13,
  output out_14,
  output out_15,
  output out_16,
  output out_17
);


  assign O = in_1[0];
  assign out_3 = in_1[1];
  assign out_4 = in_1[2];
  assign out_5 = in_1[3];
  assign out_6 = in_1[4];
  assign out_7 = in_1[5];
  assign out_8 = in_1[6];
  assign out_9 = in_1[7];
  assign out_10 = in_1[8];
  assign out_11 = in_1[9];
  assign out_12 = in_1[10];
  assign out_13 = in_1[11];
  assign out_14 = in_1[12];
  assign out_15 = in_1[13];
  assign out_16 = in_1[14];
  assign out_17 = in_1[15];
endmodule

module giant_unsplitter (
  input  O,
  input  in_2,
  input  in_3,
  input  in_4,
  input  in_5,
  input  in_6,
  input  in_7,
  input  in_8,
  input  in_9,
  input  in_10,
  input  in_11,
  input  in_12,
  input  in_13,
  input  in_14,
  input  in_15,
  input  in_16,
  output [15:0] out_17
);


  assign out_17 = {in_16, in_15, in_14, in_13, in_12, in_11, in_10, in_9, in_8, in_7, in_6, in_5, in_4, in_3, in_2, O};
endmodule

module my_comparator (
  input  Operator,
  input  [15:0] In1,
  input  [15:0] In2,
  output out_4
);

  wire multiplexer_1_out, or_1_out;
  wire [2:2] undriven;
  wire [15:0] my_alu_1_outputdata;

  Pull_Resistor #(.pull(1)) pull_resistor_1 (.node(Operator));
  my_ALU my_alu_1 (.OutputData(my_alu_1_outputdata), .InputData2(In2), .InputData1(In1), .OpType({undriven[2], 2'b01}));
  or or_1 (or_1_out, my_alu_1_outputdata[0], my_alu_1_outputdata[1], my_alu_1_outputdata[2], my_alu_1_outputdata[3], my_alu_1_outputdata[4], my_alu_1_outputdata[5], my_alu_1_outputdata[6], my_alu_1_outputdata[7], my_alu_1_outputdata[8], my_alu_1_outputdata[9], my_alu_1_outputdata[10], my_alu_1_outputdata[11], my_alu_1_outputdata[12], my_alu_1_outputdata[13], my_alu_1_outputdata[14], my_alu_1_outputdata[15]);
  Multiplexer #(.enable("false")) multiplexer_1 (
    .in0(my_alu_1_outputdata[15]), .in1(or_1_out), .out(multiplexer_1_out), .sel(Operator));
  not not_1 (out_4, multiplexer_1_out);
  // Pins of 2 and 3 bits meet at {undriven[2], 2'b01}

  // Other names for the same wires on the sheet: Op = Operator

  // Notes on the sheet:
  //   0 -> In1 >= In2
  //   1 -> In1 == In2
endmodule

module memory_latch (
  input  [15:0] address,
  input  WE,
  input  clk,
  input  [15:0] data_in,
  output [15:0] address_latched,
  output WE_latched,
  output OE_latched,
  output [15:0] data_in_latched
);

  wire DMwe_latch_q;
  wire [15:0] addr_latch_q;

  Register #(.width(16), .trigger("falling")) addr_latch (
    .D(address), .en(WE), .clk(clk), .Q(addr_latch_q));  // open: clr
  D_Flip_Flop #(.trigger("falling")) DMwe_latch (.D(WE), .clk(clk), .Q(DMwe_latch_q));  // open: Qn, preset, reset
  Register #(.width(16), .trigger("falling")) data_to_be_written (
    .D(data_in), .en(WE), .clk(clk), .Q(data_in_latched));  // open: clr
  Multiplexer #(.width(16), .enable("false")) multiplexer_1 (
    .in0(address), .in1(addr_latch_q), .out(address_latched), .sel(DMwe_latch_q));
  and and_1 (WE_latched, clk, DMwe_latch_q);
  not not_1 (OE_latched, WE_latched);
endmodule

module bit_shifter (
  input  [3:0] Shamt,
  input  Direction,
  input  [15:0] Bits,
  output [15:0] out_4
);

  wire [15:0] bit_shifter_left_1_out_3, bit_shifter_right_1_out_3;

  bit_shifter_left bit_shifter_left_1 (.in_1(Shamt), .in_2(Bits), .out_3(bit_shifter_left_1_out_3));
  bit_shifter_right bit_shifter_right_1 (.in_1(Shamt), .in_2(Bits), .out_3(bit_shifter_right_1_out_3));
  Multiplexer #(.width(16), .enable("false")) multiplexer_1 (
    .in0(bit_shifter_left_1_out_3), .in1(bit_shifter_right_1_out_3), .out(out_4), .sel(Direction));

  // Other names for the same wires on the sheet: Dir = Direction
endmodule

module bit_shifter_right (
  input  [3:0] in_1,
  input  [15:0] in_2,
  output [15:0] out_3
);

  wire [15:0] multiplexer_1_out, multiplexer_2_out, multiplexer_3_out;

  Multiplexer #(.width(16), .enable("false")) multiplexer_1 (
    .in0(in_2), .in1({{8{1'b0}}, in_2[15:8]}), .out(multiplexer_1_out), .sel(in_1[3]));
  Multiplexer #(.width(16), .enable("false")) multiplexer_2 (
    .in0(multiplexer_1_out), .in1({4'b0000, multiplexer_1_out[15:4]}), .out(multiplexer_2_out), .sel(in_1[2]));
  Multiplexer #(.width(16), .enable("false")) multiplexer_3 (
    .in0(multiplexer_2_out), .in1({2'b00, multiplexer_2_out[15:2]}), .out(multiplexer_3_out), .sel(in_1[1]));
  Multiplexer #(.width(16), .enable("false")) multiplexer_4 (
    .in0(multiplexer_3_out), .in1({1'b0, multiplexer_3_out[15:1]}), .out(out_3), .sel(in_1[0]));
endmodule

module bit_shifter_left (
  input  [3:0] in_1,
  input  [15:0] in_2,
  output [15:0] out_3
);

  wire not_1_out, not_2_out, not_3_out, not_4_out;
  wire [15:0] multiplexer_1_out, multiplexer_2_out, multiplexer_3_out;

  not not_1 (not_1_out, in_1[3]);
  Multiplexer #(.width(16), .enable("false")) multiplexer_1 (
    .in0({in_2[7:0], {8{1'b0}}}), .in1(in_2), .out(multiplexer_1_out), .sel(not_1_out));
  not not_2 (not_2_out, in_1[2]);
  Multiplexer #(.width(16), .enable("false")) multiplexer_2 (
    .in0({multiplexer_1_out[11:0], 4'b0000}), .in1(multiplexer_1_out), .out(multiplexer_2_out),
    .sel(not_2_out));
  not not_3 (not_3_out, in_1[1]);
  Multiplexer #(.width(16), .enable("false")) multiplexer_3 (
    .in0({multiplexer_2_out[13:0], 2'b00}), .in1(multiplexer_2_out), .out(multiplexer_3_out), .sel(not_3_out));
  not not_4 (not_4_out, in_1[0]);
  Multiplexer #(.width(16), .enable("false")) multiplexer_4 (
    .in0({multiplexer_3_out[14:0], 1'b0}), .in1(multiplexer_3_out), .out(out_3), .sel(not_4_out));
endmodule
