// Logisim project my_adder.circ as structural Verilog: 2 circuits, main circuit onebitadder
module my_adder (
  input  [15:0] A,
  input  [15:0] B,
  input  sub,
  output ovf,
  output [15:0] result
);

  wire multiplexer_1_out, multiplexer_2_out, multiplexer_3_out, multiplexer_4_out, multiplexer_5_out,
       multiplexer_6_out, multiplexer_7_out, multiplexer_8_out, multiplexer_9_out, multiplexer_10_out,
       multiplexer_11_out, multiplexer_12_out, multiplexer_13_out, multiplexer_14_out, multiplexer_15_out,
       multiplexer_16_out, not_1_out, not_2_out, not_3_out, not_4_out, not_5_out, not_6_out, not_7_out,
       not_8_out, not_9_out, not_10_out, not_11_out, not_12_out, not_13_out, not_14_out, not_15_out,
       not_16_out, onebitadder_1_carryout, onebitadder_3_carryout, onebitadder_4_carryout,
       onebitadder_5_carryout, onebitadder_6_carryout, onebitadder_7_carryout, onebitadder_8_carryout,
       onebitadder_9_carryout, onebitadder_10_carryout, onebitadder_11_carryout, onebitadder_12_carryout,
       onebitadder_13_carryout, onebitadder_14_carryout, onebitadder_15_carryout, onebitadder_16_carryout,
       over1;

  not not_1 (not_1_out, B[15]);
  not not_2 (not_2_out, B[14]);
  not not_3 (not_3_out, B[13]);
  not not_4 (not_4_out, B[12]);
  not not_5 (not_5_out, B[11]);
  not not_6 (not_6_out, B[10]);
  not not_7 (not_7_out, B[9]);
  not not_8 (not_8_out, B[8]);
  not not_9 (not_9_out, B[7]);
  not not_10 (not_10_out, B[6]);
  not not_11 (not_11_out, B[5]);
  not not_12 (not_12_out, B[4]);
  not not_13 (not_13_out, B[3]);
  not not_14 (not_14_out, B[2]);
  not not_15 (not_15_out, B[1]);
  not not_16 (not_16_out, B[0]);
  Multiplexer #(.enable("false")) multiplexer_1 (.in0(B[15]), .in1(not_1_out), .out(multiplexer_1_out), .sel(sub));
  Multiplexer #(.enable("false")) multiplexer_2 (.in0(B[14]), .in1(not_2_out), .out(multiplexer_2_out), .sel(sub));
  Multiplexer #(.enable("false")) multiplexer_3 (.in0(B[13]), .in1(not_3_out), .out(multiplexer_3_out), .sel(sub));
  Multiplexer #(.enable("false")) multiplexer_4 (.in0(B[12]), .in1(not_4_out), .out(multiplexer_4_out), .sel(sub));
  Multiplexer #(.enable("false")) multiplexer_5 (.in0(B[11]), .in1(not_5_out), .out(multiplexer_5_out), .sel(sub));
  Multiplexer #(.enable("false")) multiplexer_6 (.in0(B[10]), .in1(not_6_out), .out(multiplexer_6_out), .sel(sub));
  Multiplexer #(.enable("false")) multiplexer_7 (.in0(B[9]), .in1(not_7_out), .out(multiplexer_7_out), .sel(sub));
  Multiplexer #(.enable("false")) multiplexer_8 (.in0(B[8]), .in1(not_8_out), .out(multiplexer_8_out), .sel(sub));
  Multiplexer #(.enable("false")) multiplexer_9 (.in0(B[7]), .in1(not_9_out), .out(multiplexer_9_out), .sel(sub));
  Multiplexer #(.enable("false")) multiplexer_10 (.in0(B[6]), .in1(not_10_out), .out(multiplexer_10_out), .sel(sub));
  Multiplexer #(.enable("false")) multiplexer_11 (.in0(B[5]), .in1(not_11_out), .out(multiplexer_11_out), .sel(sub));
  Multiplexer #(.enable("false")) multiplexer_12 (.in0(B[4]), .in1(not_12_out), .out(multiplexer_12_out), .sel(sub));
  Multiplexer #(.enable("false")) multiplexer_13 (.in0(B[3]), .in1(not_13_out), .out(multiplexer_13_out), .sel(sub));
  Multiplexer #(.enable("false")) multiplexer_14 (.in0(B[2]), .in1(not_14_out), .out(multiplexer_14_out), .sel(sub));
  Multiplexer #(.enable("false")) multiplexer_15 (.in0(B[1]), .in1(not_15_out), .out(multiplexer_15_out), .sel(sub));
  Multiplexer #(.enable("false")) multiplexer_16 (.in0(B[0]), .in1(not_16_out), .out(multiplexer_16_out), .sel(sub));
  onebitadder onebitadder_1 (
    .carryout(onebitadder_1_carryout), .output0(result[15]), .carryin(over1), .input1(multiplexer_1_out),
    .input0(A[15]));
  onebitadder onebitadder_2 (
    .carryout(over1), .output0(result[14]), .carryin(onebitadder_3_carryout), .input1(multiplexer_2_out),
    .input0(A[14]));
  onebitadder onebitadder_3 (
    .carryout(onebitadder_3_carryout), .output0(result[13]), .carryin(onebitadder_4_carryout),
    .input1(multiplexer_3_out), .input0(A[13]));
  onebitadder onebitadder_4 (
    .carryout(onebitadder_4_carryout), .output0(result[12]), .carryin(onebitadder_5_carryout),
    .input1(multiplexer_4_out), .input0(A[12]));
  onebitadder onebitadder_5 (
    .carryout(onebitadder_5_carryout), .output0(result[11]), .carryin(onebitadder_6_carryout),
    .input1(multiplexer_5_out), .input0(A[11]));
  onebitadder onebitadder_6 (
    .carryout(onebitadder_6_carryout), .output0(result[10]), .carryin(onebitadder_7_carryout),
    .input1(multiplexer_6_out), .input0(A[10]));
  onebitadder onebitadder_7 (
    .carryout(onebitadder_7_carryout), .output0(result[9]), .carryin(onebitadder_8_carryout),
    .input1(multiplexer_7_out), .input0(A[9]));
  onebitadder onebitadder_8 (
    .carryout(onebitadder_8_carryout), .output0(result[8]), .carryin(onebitadder_9_carryout),
    .input1(multiplexer_8_out), .input0(A[8]));
  onebitadder onebitadder_9 (
    .carryout(onebitadder_9_carryout), .output0(result[7]), .carryin(onebitadder_10_carryout),
    .input1(multiplexer_9_out), .input0(A[7]));
  onebitadder onebitadder_10 (
    .carryout(onebitadder_10_carryout), .output0(result[6]), .carryin(onebitadder_11_carryout),
    .input1(multiplexer_10_out), .input0(A[6]));
  onebitadder onebitadder_11 (
    .carryout(onebitadder_11_carryout), .output0(result[5]), .carryin(onebitadder_12_carryout),
    .input1(multiplexer_11_out), .input0(A[5]));
  onebitadder onebitadder_12 (
    .carryout(onebitadder_12_carryout), .output0(result[4]), .carryin(onebitadder_13_carryout),
    .input1(multiplexer_12_out), .input0(A[4]));
  onebitadder onebitadder_13 (
    .carryout(onebitadder_13_carryout), .output0(result[3]), .carryin(onebitadder_14_carryout),
    .input1(multiplexer_13_out), .input0(A[3]));
  onebitadder onebitadder_14 (
    .carryout(onebitadder_14_carryout), .output0(result[2]), .carryin(onebitadder_15_carryout),
    .input1(multiplexer_14_out), .input0(A[2]));
  onebitadder onebitadder_15 (
    .carryout(onebitadder_15_carryout), .output0(result[1]), .carryin(onebitadder_16_carryout),
    .input1(multiplexer_15_out), .input0(A[1]));
  onebitadder onebitadder_16 (
    .carryout(onebitadder_16_carryout), .output0(result[0]), .carryin(sub), .input1(multiplexer_16_out),
    .input0(A[0]));
  xor xor_1 (ovf, over1, onebitadder_1_carryout);
endmodule

module onebitadder (
  input  input0,
  input  input1,
  input  carryin,
  output output0,
  output carryout
);

  wire and_1_out, and_2_out, and_3_out;

  and and_1 (and_1_out, input0, carryin);
  and and_2 (and_2_out, input0, input1);
  and and_3 (and_3_out, input1, carryin);
  xor xor_1 (output0, input0, input1, carryin);
  or or_1 (carryout, and_1_out, and_2_out, and_3_out);
endmodule
